// Digital circuit state_machine_digital.dig as structural Verilog
module state_machine_digital (
  input  photocell2,
  input  photocell3,
  input  photocell4,
  input  clk,
  input  [1:0] in_14,
  input  photocell1,
  output out_3,
  output out_4,
  output out_5,
  output out_6,
  output out_7,
  output out_9,
  output [5:0] out_10,
  output [5:0] out_11,
  output out_12,
  output [7:0] out_15,
  output [7:0] out_16,
  output out_17
);

  wire u_tof_mimic_tof1, u_tof_mimic_tof2, u_tof_mimic_tof3, u_tof_mimic_tof4;
  wire [7:0] u_RegistroIncDec8bit_q;

  tof_mimic #(.applicationType("GHDL")) u_tof_mimic (
    .mv_msg(u_RegistroIncDec8bit_q), .i1(photocell1), .i2(photocell2), .i3(photocell3), .i4(photocell4),
    .tof1(u_tof_mimic_tof1), .tof2(u_tof_mimic_tof2), .tof3(u_tof_mimic_tof3), .tof4(u_tof_mimic_tof4));
  decoder_5_6 #(.applicationType("GHDL"), .Code_File("C:\\Users\\davol\\embedded_system_design\\digital\\src\\encoder_4_2.vhd")) u_decoder_5_6 (
    .i1(u_tof_mimic_tof1), .i2(u_tof_mimic_tof2), .i3(u_tof_mimic_tof3), .i4(u_tof_mimic_tof4),
    .msg(u_RegistroIncDec8bit_q), .o1(out_3), .o2(out_4), .o3(out_5), .o4(out_6), .mv(out_7), .pr(out_9),
    .err(out_10[5]));
  RegistroIncDec8bit #(.applicationType("GHDL")) u_RegistroIncDec8bit (
    .D(out_15), .Set(out_17), .Inc(1'b0), .Dec(1'b0), .Clk(clk), .Reset(1'b0), .Q(u_RegistroIncDec8bit_q));
  write_uart_sm #(.applicationType("GHDL"), .Code_File("C:\\Users\\davol\\embedded_system_design\\digital\\src\\write_uart_state_machine.vhd")) u_write_uart_sm (
    .state_vector({out_10[5], out_9, out_7, out_5, out_4, out_3}), .ext_error(out_10[5]), .clk(clk),
    .data_write(out_11), .data_write_bool(out_12));
  // ComPort #(.comPort("COM6")) COM6: pin names not known; wires that end beside it: {in_14, out_11}, out_12, 1'b1, clk, out_15, out_17

  assign out_10[4:0] = {out_9, out_7, out_5, out_4, out_3};
  assign out_16 = {in_14, out_11};

  // Notes on the sheet:
  //   clk: Hz: 50000
  //   in_14: default 1
endmodule

/* Code of tof_mimic:
library ieee;
use ieee.std_logic_1164.all;

entity tof_mimic is
	port ( i1, i2, i3, i4: in std_logic;
           mv_msg: in std_logic_vector(7 downto 0);
	       tof1, tof2, tof3, tof4: out std_logic);
end entity tof_mimic;

architecture arc_tof_mimic of tof_mimic is
    signal mv_counter: std_logic;
begin
    comb: process(mv_counter, i1, i2, i3, i4)
    begin
        tof1 <= i1;
        tof2 <= i2;
        tof3 <= i3;
        tof4 <= i4;
        if (mv_counter) then
            tof1 <= '0';
            tof2 <= '0';
            tof3 <= '0';
            tof4 <= '0';
        end if;
    end process;

    upd: process(mv_msg, i1, i2, i3, i4)
    begin
        if (mv_msg = "01001000" and mv_msg'event) then
            mv_counter <= '1';
        elsif (i1'event and i1 = '0') then
            mv_counter <= '0';
        elsif (i2'event and i2 = '0') then
            mv_counter <= '0';
        elsif (i3'event and i3 = '0') then
            mv_counter <= '0';
        elsif (i4'event and i4 = '0') then
            mv_counter <= '0';
        end if;
    end process;
end arc_tof_mimic;
*/

/* Code of decoder_5_6:
library ieee;
use ieee.std_logic_1164.all;

entity decoder_5_6 is
	port ( i1, i2, i3, i4: in std_logic;
           msg: in std_logic_vector(7 downto 0);
	       o1, o2, o3, o4, mv, pr, err: out std_logic);
end entity decoder_5_6;

architecture arc_decoder_5_6 of decoder_5_6 is
    signal idle: std_logic;
begin
    process(msg) is
    begin
        pr <= '0';
        idle <= '0';
        if (msg = "01010000") then
            pr <= '1';
        elsif (msg = "00000000") then
            idle <= '1';
        end if;
    end process;

    process(i1, i2, i3, i4, pr, idle) is
        variable combined_input: std_logic_vector(4 downto 0);
    begin
        combined_input := pr & i4 & i3 & i2 & i1;
        o1 <= '0';
        o2 <= '0';
        o3 <= '0';
        o4 <= '0';
        mv <= '0';
        pr <= '0';
        err <= '0';
        case combined_input is
            when "00001" =>
                o1 <= '1';
            when "00010" =>
                o2 <= '1';
            when "00100" =>
                o3 <= '1';
            when "01000" =>
                o4 <= '1';
            when "00000" =>
                if (idle = '0') then
                    mv <= '1';
                else
                    mv <= '0';
                end if;
            when "10000" | "10010" | "10100" | "11000" =>
                pr <= '1';
            when others =>
                err <= '1';
        end case;
    end process;
end arc_decoder_5_6;
*/

/* Code of RegistroIncDec8bit:
library ieee;
use ieee.std_logic_1164.all;
use ieee.numeric_std.all;
-- per dare un senso agli operatori +1 e -1:
use ieee.std_logic_unsigned.all; 


entity RegistroIncDec8bit is

	port 
	(
		Q : out  std_logic_vector(7 downto 0);
		D : in  std_logic_vector(7 downto 0);
		Set: in std_logic;
		Inc: in std_logic;
		Dec: in std_logic;
		Clk : in std_logic;
		Reset : in std_logic
	);

end RegistroIncDec8bit;
architecture behav of RegistroIncDec8bit is
signal currVal  :  std_logic_vector(7 downto 0);
signal nextVal :  std_logic_vector(7 downto 0);
signal IncDecSet :  std_logic_vector(2 downto 0); -- segnale ausiliario
begin

	process(clk)
	begin
		if (clk='1' and clk'event) then
			if (reset ='1') then	
				currVal <= (others =>'0');
			else
				currVal <= nextVal;
			end if;
		end if;
	end process;
	
	-- selezione del prossimo valore interno
	IncDecSet <= Inc & Dec & Set;
	with IncDecSet select
		nextVal <= D		when "001",
			   currVal + 1  when "100",
			   currVal - 1  when "010",
			   currVal		when others;  -- others assures combinatorial synthesis	
			   				  
	Q <= currVal;

end behav;
*/

/* Code of write_uart_sm:
library ieee;
use ieee.std_logic_1164.all;

entity write_uart_sm is
	port ( state_vector: in std_logic_vector(5 downto 0);
           ext_error: in std_logic;
           clk: in std_logic;
	       data_write: out std_logic_vector(5 downto 0); 
           data_write_bool: out std_logic);
end entity write_uart_sm;

architecture arc_write_uart_sm of write_uart_sm is
    signal state_changed: std_logic;
    signal current_state: std_logic_vector(5 downto 0);
begin
    process(clk) is
    begin
        if (clk = '1' and clk'event) then
            data_write <= state_vector;
            if (state_vector /= current_state and ext_error = '0') then
                state_changed <= '1';
                current_state <= state_vector;
                data_write_bool <= '1';
            else
                data_write_bool <= '0';
            end if;
        end if;
    end process;
end arc_write_uart_sm;
*/
